# Fritzing sketch sketch (saved by Fritzing 0.9.6b)
breadboards: 1

parts:
  Part1 = Arduino Nano (Rev3.0)
  Part2 = Barometric Pressure Sensor - BMP180 Breakout (GY-68)
  Part3 = InvenSense MPU6050
  microSD1 = MicroSD Card Module
  LED1 = LED - 5mm [color="Red (633nm)" current=0.030 package="5 mm [THT]"]
  LED2 = LED - 5mm [color="Green (570nm)" current=0.030 package="5 mm [THT]"]
  LED3 = LED - 5mm [color="Blue (525nm)" current=0.030 package="5 mm [THT]"]
  R1 = Resistor [tolerance=±5% power=0.25 resistance=220 package=THT]
  J1 = Piezo Speaker

nets:
  GND: Part1.D6, Part2.GND, Part3.GND, microSD1.GND, R1.Pin_0, J1.pin1, J1.pin2
  N1: Part1.D7, LED3.anode
  N2: Part1.D8, LED2.anode
  N3: Part1.D9, LED1.anode
  N4: Part1.D10, microSD1.CS
  N5: Part1.D11/MOSI, microSD1.MOSI
  N6: Part1.D12/MISO, microSD1.MISO
  N7: Part1.A5, Part2.SCL, Part3.SCL
  N8: Part1.A4, Part2.SDA, Part3.SDA
  N9: Part1.D13/SCK, microSD1.SCK
  VCC: Part2.VCC, Part3.VCC, microSD1.VCC
  N10: LED1.cathode, LED2.cathode, LED3.cathode, R1.Pin_1
